// Logisim project task2_grayBCD.circ as structural Verilog: 1 circuit, main circuit main
module main (
  input  X3,
  input  X2,
  input  X1,
  input  X0,
  output P,
  output Y3,
  output Y2,
  output Y1,
  output Y0
);

  wire and_1_out, and_2_out, and_3_out, and_4_out, and_5_out, and_6_out, and_7_out, and_8_out, and_9_out,
       not_1_out, not_2_out, not_3_out, not_4_out;

  not not_1 (not_1_out, X3);
  not not_2 (not_2_out, X2);
  not not_3 (not_3_out, X1);
  not not_4 (not_4_out, X0);
  or or_1 (P, X0, X1, X2);
  and and_1 (and_1_out, not_4_out, not_3_out, not_2_out);
  and and_2 (and_2_out, X3, X0);
  and and_3 (and_3_out, not_4_out, not_3_out);
  and and_4 (and_4_out, X0, X2);
  and and_5 (and_5_out, X0, X2, not_1_out);
  and and_6 (and_6_out, not_4_out, X1);
  and and_7 (and_7_out, X1, not_2_out);
  and and_8 (and_8_out, not_3_out, X2, not_1_out);
  and and_9 (and_9_out, not_4_out, not_3_out, not_1_out);
  or or_2 (Y3, and_1_out, and_2_out);
  or or_3 (Y2, and_3_out, and_4_out);
  or or_4 (Y1, and_5_out, and_6_out);
  or or_5 (Y0, and_7_out, and_8_out, and_9_out);
endmodule
