// Logisim project task3_t_trigger.circ as structural Verilog: 1 circuit, main circuit main
module main (
  input  in_1,
  output out_2,
  output out_3,
  output out_4
);

  wire clock_1_out, nand_1_out, nand_2_out;

  T_Flip_Flop t_ff_1 (.T(in_1), .clk(clock_1_out), .Q(out_2));  // open: Qn, reset, preset
  Clock clock_1 (.out(clock_1_out));
  T_Flip_Flop t_ff_2 (.T(out_2), .clk(clock_1_out), .Q(out_3));  // open: Qn, reset, preset
  nand nand_1 (nand_1_out, out_2, out_3);
  nand nand_2 (nand_2_out, nand_1_out, nand_1_out);
  T_Flip_Flop t_ff_3 (.T(nand_2_out), .clk(clock_1_out), .Q(out_4));  // open: Qn, reset, preset
endmodule
